// Logisim project syslo_proj_V4.circ as structural Verilog: 13 circuits, main circuit main
module main (
  input  direction_switch,
  input  alarm_active,
  input  local_timer_reset,
  input  MISO,
  input  ACCEL_INT,
  input  ENABLE_ACCEL,
  output MOSI,
  output SCKL,
  output CS,
  output buzzer_signal
);

  wire action_button_out, alarm_module_1_alarm_end, clock_1_out, clock_2_out, clock_3_out, clock_4_out,
       clock_5_out, countdown_module_1_countdown_end,
       countdown_run_enable_sequential_logic_1_countdown_run_enable, display_mux_1_flash_1,
       display_mux_1_flash_2, global_reset_out, mode_button_out, SR_Pulse_1_o, SR_Sync_1_o, undriven,
       undriven_2, undriven_3;
  wire [1:0] display_mux_1_alarm_countdown_end, display_mux_1_display_mode,
       fsm_state_decoder_1_set_clock_hours_mode, fsm_state_decoder_1_timer_idle_mode;
  wire [2:0] fsm_state_decoder_1_set_alarm_minutes_mode;
  wire [3:0] alarm_module_1_hours_tens, alarm_module_1_hours_units, alarm_module_1_minutes_tens,
       alarm_module_1_minutes_units, countdown_module_1_minutes_tens, countdown_module_1_minutes_units,
       countdown_module_1_seconds_tens, countdown_module_1_seconds_units, FSM_transition_logic_1_q0n,
       hour_module_1_hours_tens, hour_module_1_hours_units, hour_module_1_minutes_tens,
       hour_module_1_minutes_units, register_1_q, timer_module_1_minutes_tens, timer_module_1_minutes_units,
       timer_module_1_seconds_tens, timer_module_1_seconds_units;
  wire [4:0] fsm_state_decoder_1_countdown_set_minutes_mode;
  wire [10:0] hour_module_1_current_time;
  wire [15:0] display_mux_1_display_signal;
  wire [41:0] display;

  Button global_reset (.out(global_reset_out));
  // OR_Gate or_1 has open pins: in0=undriven_2, in1=undriven, out=open
  _7_Segment_Display u_7_segment_display_1 (
    .g(display[35]), .f(display[36]), .a(display[37]), .b(display[38]), .e(display[41]), .d(display[40]),
    .c(display[39]));  // open: dp
  _7_Segment_Display u_7_segment_display_2 (
    .g(display[28]), .f(display[29]), .a(display[30]), .b(display[31]), .e(display[34]), .d(display[33]),
    .c(display[32]));  // open: dp
  _7_Segment_Display u_7_segment_display_3 (
    .g(display[14]), .f(display[15]), .a(display[16]), .b(display[17]), .e(display[20]), .d(display[19]),
    .c(display[18]));  // open: dp
  _7_Segment_Display u_7_segment_display_4 (
    .g(display[21]), .f(display[22]), .a(display[23]), .b(display[24]), .e(display[27]), .d(display[26]),
    .c(display[25]));  // open: dp
  _7_Segment_Display u_7_segment_display_5 (
    .g(display[0]), .f(display[1]), .a(display[2]), .b(display[3]), .e(display[6]), .d(display[5]),
    .c(display[4]));  // open: dp
  _7_Segment_Display u_7_segment_display_6 (
    .g(display[7]), .f(display[8]), .a(display[9]), .b(display[10]), .e(display[13]), .d(display[12]),
    .c(display[11]));  // open: dp
  Button action_button (.out(action_button_out));
  Button mode_button (.out(mode_button_out));
  Clock #(.highDuration(4), .lowDuration(4)) clock_1 (.out(clock_1_out));
  Clock #(.highDuration(2), .lowDuration(2)) clock_2 (.out(clock_2_out));
  Clock clock_3 (.out(clock_3_out));
  Clock #(.highDuration(8), .lowDuration(56)) clock_4 (.out(clock_4_out));
  SR_Sync SR_Sync_1 (
    .O(SR_Sync_1_o), .S(action_button_out), .global_reset(global_reset_out), .high_clock(clock_3_out),
    .low_clock(clock_2_out));
  SR_Pulse SR_Pulse_1 (
    .O(SR_Pulse_1_o), .global_reset(global_reset_out), .S(mode_button_out), .high_clock(clock_3_out),
    .low_clock(clock_1_out));
  FSM_transition_logic FSM_transition_logic_1 (
    .Q3(register_1_q[3]), .Q2(register_1_q[2]), .Q1(register_1_q[1]), .Q0(register_1_q[0]),
    .EAM(alarm_module_1_alarm_end), .CF(countdown_module_1_countdown_end), .S(undriven_3), .A(SR_Sync_1_o),
    .M(SR_Pulse_1_o), .Q3N(FSM_transition_logic_1_q0n[3]), .Q2N(FSM_transition_logic_1_q0n[2]),
    .Q1N(FSM_transition_logic_1_q0n[1]), .Q0N(FSM_transition_logic_1_q0n[0]));
  Register #(.width(4)) register_1 (
    .D(FSM_transition_logic_1_q0n), .clk(clock_1_out), .Q(register_1_q), .clr(global_reset_out));  // open: en
  countdown_run_enable_sequential_logic countdown_run_enable_sequential_logic_1 (
    .next_mode(FSM_transition_logic_1_q0n),
    .countdown_run_mode(fsm_state_decoder_1_countdown_set_minutes_mode[3]), .SIXTEEN_Hz_clock(clock_1_out),
    .global_reset(global_reset_out),
    .countdown_run_enable(countdown_run_enable_sequential_logic_1_countdown_run_enable));
  fsm_state_decoder fsm_state_decoder_1 (
    .fsm_state_endoding(register_1_q), .set_clock_hours_mode(fsm_state_decoder_1_set_clock_hours_mode[0]),
    .set_clock_minutes_mode(fsm_state_decoder_1_set_clock_hours_mode[1]),
    .set_alarm_hours_mode(fsm_state_decoder_1_set_alarm_minutes_mode[1]),
    .set_alarm_minutes_mode(fsm_state_decoder_1_set_alarm_minutes_mode[0]),
    .timer_idle_mode(fsm_state_decoder_1_timer_idle_mode[0]),
    .timer_run_mode(fsm_state_decoder_1_timer_idle_mode[1]),
    .countdown_set_minutes_mode(fsm_state_decoder_1_countdown_set_minutes_mode[0]),
    .countdown_set_seconds_mode(fsm_state_decoder_1_countdown_set_minutes_mode[1]),
    .countdown_idle_mode(fsm_state_decoder_1_countdown_set_minutes_mode[2]),
    .countdown_run_mode(fsm_state_decoder_1_countdown_set_minutes_mode[3]),
    .countdown_end_mode(fsm_state_decoder_1_countdown_set_minutes_mode[4]),
    .alarm_reached_mode(fsm_state_decoder_1_set_alarm_minutes_mode[2]));  // open: clock_mode
  hour_module hour_module_1 (
    .action_button(SR_Sync_1_o), .direction_switch(direction_switch),
    .hours_set_enable(fsm_state_decoder_1_set_clock_hours_mode[0]),
    .minutes_set_enable(fsm_state_decoder_1_set_clock_hours_mode[1]), .global_reset(global_reset_out),
    .ONE_Hz_clock(clock_4_out), .SIXTEEN_Hz_clock(clock_1_out), .current_time(hour_module_1_current_time),
    .minutes_tens(hour_module_1_minutes_tens), .minutes_units(hour_module_1_minutes_units),
    .hours_tens(hour_module_1_hours_tens), .hours_units(hour_module_1_hours_units));
  alarm_module alarm_module_1 (
    .action_button(SR_Sync_1_o), .direction_switch(direction_switch), .alarm_active(alarm_active),
    .current_time(hour_module_1_current_time),
    .hours_set_enable(fsm_state_decoder_1_set_alarm_minutes_mode[1]),
    .minutes_set_enable(fsm_state_decoder_1_set_alarm_minutes_mode[0]), .global_reset(global_reset_out),
    .SIXTEEN_Hz_clock(clock_1_out), .alarm_end(alarm_module_1_alarm_end),
    .minutes_tens(alarm_module_1_minutes_tens), .minutes_units(alarm_module_1_minutes_units),
    .hours_tens(alarm_module_1_hours_tens), .hours_units(alarm_module_1_hours_units));
  timer_module timer_module_1 (
    .timer_run_enable(fsm_state_decoder_1_timer_idle_mode[1]), .local_reset_switch(local_timer_reset),
    .global_reset(global_reset_out), .ONE_Hz_clock(clock_4_out), .seconds_tens(timer_module_1_seconds_tens),
    .seconds_units(timer_module_1_seconds_units), .minutes_tens(timer_module_1_minutes_tens),
    .minutes_units(timer_module_1_minutes_units));
  countdown_module countdown_module_1 (
    .action_button(SR_Sync_1_o), .direction_switch(direction_switch),
    .minutes_set_enable(fsm_state_decoder_1_countdown_set_minutes_mode[0]),
    .seconds_set_enable(fsm_state_decoder_1_countdown_set_minutes_mode[1]),
    .countdown_run_enable(countdown_run_enable_sequential_logic_1_countdown_run_enable),
    .global_reset(global_reset_out), .ONE_Hz_clock(clock_4_out), .SIXTEEN_Hz_clock(clock_1_out),
    .countdown_end(countdown_module_1_countdown_end), .seconds_tens(countdown_module_1_seconds_tens),
    .seconds_units(countdown_module_1_seconds_units), .minutes_tens(countdown_module_1_minutes_tens),
    .minutes_units(countdown_module_1_minutes_units));
  buzzer_module buzzer_module_1 (
    .alarm_reached_mode(fsm_state_decoder_1_set_alarm_minutes_mode[2]),
    .countdown_end_mode(fsm_state_decoder_1_countdown_set_minutes_mode[4]), .buzzer_signal(buzzer_signal));
  Clock #(.highDuration(32), .lowDuration(32)) clock_5 (.out(clock_5_out));
  display_mux display_mux_1 (
    .hour_in({hour_module_1_hours_units, hour_module_1_hours_tens, hour_module_1_minutes_units, hour_module_1_minutes_tens}),
    .alarm_in({alarm_module_1_hours_units, alarm_module_1_hours_tens, alarm_module_1_minutes_units, alarm_module_1_minutes_tens}),
    .timer_in({timer_module_1_minutes_units, timer_module_1_minutes_tens, timer_module_1_seconds_units, timer_module_1_seconds_tens}),
    .countdown_in({countdown_module_1_minutes_units, countdown_module_1_minutes_tens, countdown_module_1_seconds_units, countdown_module_1_seconds_tens}),
    .countdown_modes(fsm_state_decoder_1_countdown_set_minutes_mode),
    .timer_modes(fsm_state_decoder_1_timer_idle_mode),
    .alarm_modes(fsm_state_decoder_1_set_alarm_minutes_mode),
    .hour_modes(fsm_state_decoder_1_set_clock_hours_mode), .flash_clock(clock_5_out),
    .action(action_button_out), .display_signal(display_mux_1_display_signal),
    .display_mode(display_mux_1_display_mode), .alarm_countdown_end(display_mux_1_alarm_countdown_end),
    .flash_2(display_mux_1_flash_2), .flash_1(display_mux_1_flash_1));
  display_module display_module_1 (
    .tens_2nd(display_mux_1_display_signal[3:0]), .units_2nd(display_mux_1_display_signal[7:4]),
    .tens_1st(display_mux_1_display_signal[11:8]), .units_1st(display_mux_1_display_signal[15:12]),
    .display_mode(display_mux_1_display_mode), .alarm_countdown_end(display_mux_1_alarm_countdown_end),
    .flash_2(display_mux_1_flash_2), .flash_1(display_mux_1_flash_1), .tens_2nd_7dig(display[6:0]),
    .units_2nd_7dig(display[13:7]), .tens_1st_7dig(display[20:14]), .units_1st_7dig(display[27:21]),
    .label_2nd(display[34:28]), .label_1st(display[41:35]));

  // Notes on the sheet:
  //   64000
  //   32000
  //   16000
  //   128000
  //   896000
  //   16Hz
  //   32Hz
  //   64Hz
  //   1 Hz tick
  //   current state
  //   512000
endmodule

module FSM_transition_logic (
  input  Q3,
  input  Q2,
  input  Q1,
  input  Q0,
  input  EAM,
  input  CF,
  input  S,
  input  A,
  input  M,
  output Q3N,
  output Q2N,
  output Q1N,
  output Q0N
);

  wire and_1_out, and_2_out, and_3_out, and_4_out, and_5_out, and_6_out, and_7_out, and_8_out, and_9_out,
       and_10_out, and_11_out, and_12_out, and_13_out, and_14_out, and_15_out, and_16_out, and_17_out,
       and_18_out, and_19_out, and_20_out, and_21_out, and_22_out, and_23_out, and_24_out, and_25_out,
       and_26_out, and_27_out, and_28_out, and_29_out, and_30_out, and_31_out, and_32_out, and_33_out,
       and_34_out, and_35_out, and_36_out, and_37_out, and_38_out, and_39_out, and_40_out, and_41_out,
       and_42_out, and_43_out, and_44_out, and_45_out, and_46_out, and_47_out, and_48_out, and_49_out,
       and_50_out, and_51_out, and_52_out, and_53_out, and_54_out, and_55_out, and_56_out, not_1_out,
       not_2_out, not_3_out, not_4_out, not_5_out, not_6_out, not_7_out, not_8_out, not_9_out;

  not not_1 (not_1_out, EAM);
  not not_2 (not_2_out, CF);
  not not_3 (not_3_out, S);
  not not_4 (not_4_out, A);
  not not_5 (not_5_out, M);
  not not_6 (not_6_out, Q3);
  not not_7 (not_7_out, Q2);
  not not_8 (not_8_out, Q1);
  not not_9 (not_9_out, Q0);
  and and_1 (and_1_out, not_3_out, not_4_out, not_5_out, Q3);
  and and_2 (and_2_out, Q3, not_7_out, not_8_out, not_9_out);
  and and_3 (and_3_out, not_5_out, Q3, not_8_out, Q0);
  and and_4 (and_4_out, not_5_out, Q3, Q1, not_9_out);
  and and_5 (and_5_out, M, Q2, Q1, Q0);
  and and_6 (and_6_out, A, Q3, not_8_out, Q0);
  and and_7 (and_7_out, A, Q3, Q1, not_9_out);
  and and_8 (and_8_out, CF, not_6_out);
  and and_9 (and_9_out, CF, not_7_out, not_9_out);
  and and_10 (and_10_out, CF, not_8_out, Q0);
  and and_11 (and_11_out, EAM, not_6_out);
  and and_12 (and_12_out, EAM, not_7_out, not_9_out);
  and and_13 (and_13_out, EAM, not_8_out, Q0);
  and and_14 (and_14_out, not_2_out, not_6_out, Q2, not_9_out);
  and and_15 (and_15_out, not_2_out, Q2, not_8_out, Q0);
  and and_16 (and_16_out, not_2_out, not_5_out, Q2, Q1);
  and and_17 (and_17_out, not_2_out, Q2, Q1, not_9_out);
  and and_18 (and_18_out, not_3_out, not_4_out, not_5_out, Q3, Q2);
  and and_19 (and_19_out, not_2_out, M, not_6_out, not_7_out, Q1, Q0);
  and and_20 (and_20_out, not_3_out, A, Q3, Q1, Q0);
  and and_21 (and_21_out, EAM, not_6_out);
  and and_22 (and_22_out, EAM, not_7_out, not_9_out);
  and and_23 (and_23_out, EAM, not_8_out, Q0);
  and and_24 (and_24_out, not_1_out, not_4_out, not_5_out, Q1, not_9_out);
  and and_25 (and_25_out, not_1_out, not_6_out, not_7_out, Q1, not_9_out);
  and and_26 (and_26_out, not_1_out, not_3_out, not_5_out, Q1, Q0);
  and and_27 (and_27_out, not_1_out, not_5_out, not_6_out, Q1, Q0);
  and and_28 (and_28_out, not_1_out, not_4_out, Q2, Q1, not_9_out);
  and and_29 (and_29_out, not_3_out, not_5_out, Q3, Q1, Q0);
  and and_30 (and_30_out, not_1_out, M, not_6_out, not_8_out, Q0);
  and and_31 (and_31_out, not_1_out, A, not_5_out, Q2, Q0);
  and and_32 (and_32_out, not_1_out, not_3_out, A, Q3, Q0);
  and and_33 (and_33_out, not_1_out, A, Q3, not_8_out, Q0);
  and and_34 (and_34_out, not_3_out, A, Q3, Q1, Q0);
  and and_35 (and_35_out, not_3_out, A, Q3, Q2);
  and and_36 (and_36_out, not_1_out, CF, not_6_out);
  and and_37 (and_37_out, not_1_out, CF, not_7_out, not_9_out);
  and and_38 (and_38_out, not_1_out, CF, not_8_out, Q0);
  and and_39 (and_39_out, not_1_out, not_4_out, not_5_out, not_8_out, Q0);
  and and_40 (and_40_out, not_1_out, not_5_out, not_6_out, not_7_out, Q0);
  and and_41 (and_41_out, not_1_out, not_3_out, not_5_out, Q1, Q0);
  and and_42 (and_42_out, not_1_out, not_4_out, Q2, not_8_out, Q0);
  and and_43 (and_43_out, not_1_out, not_5_out, Q2, Q1, Q0);
  and and_44 (and_44_out, not_3_out, not_5_out, Q3, Q1, Q0);
  and and_45 (and_45_out, not_1_out, M, not_6_out, not_9_out);
  and and_46 (and_46_out, not_1_out, M, not_7_out, not_8_out, not_9_out);
  and and_47 (and_47_out, not_1_out, A, not_5_out, Q2, Q1);
  and and_48 (and_48_out, not_1_out, not_3_out, A, Q3, Q1);
  and and_49 (and_49_out, not_1_out, A, Q3, Q1, not_9_out);
  and and_50 (and_50_out, not_3_out, A, Q3, Q1, Q0);
  and and_51 (and_51_out, not_3_out, A, Q3, Q2);
  and and_52 (and_52_out, not_1_out, CF, not_6_out);
  and and_53 (and_53_out, not_1_out, CF, not_7_out, not_8_out);
  and and_54 (and_54_out, not_1_out, CF, not_7_out, not_9_out);
  and and_55 (and_55_out, not_1_out, CF, Q1, not_9_out);
  and and_56 (and_56_out, not_1_out, CF, not_3_out, A);
  or or_1 (Q3N, and_1_out, and_2_out, and_3_out, and_4_out, and_5_out, and_6_out, and_7_out, and_8_out, and_9_out, and_10_out, and_11_out, and_12_out, and_13_out);
  or or_2 (Q2N, and_14_out, and_15_out, and_16_out, and_17_out, and_18_out, and_19_out, and_20_out, and_21_out, and_22_out, and_23_out);
  or or_3 (Q1N, and_24_out, and_25_out, and_26_out, and_27_out, and_28_out, and_29_out, and_30_out, and_31_out, and_32_out, and_33_out, and_34_out, and_35_out, and_36_out, and_37_out, and_38_out);
  or or_4 (Q0N, and_39_out, and_40_out, and_41_out, and_42_out, and_43_out, and_44_out, and_45_out, and_46_out, and_47_out, and_48_out, and_49_out, and_50_out, and_51_out, and_52_out, and_53_out, and_54_out, and_55_out, and_56_out);
endmodule

module hour_module (
  input  action_button,
  input  direction_switch,
  input  hours_set_enable,
  input  minutes_set_enable,
  input  global_reset,
  input  ONE_Hz_clock,
  input  SIXTEEN_Hz_clock,
  output [10:0] current_time,
  output [3:0] minutes_tens,
  output [3:0] minutes_units,
  output [3:0] hours_tens,
  output [3:0] hours_units
);

  wire and_1_out, and_2_out, and_3_out, and_4_out, counter_2_carry, nand_1_out, or_1_out, or_2_out, or_3_out,
       seconds_carry;

  or or_1 (or_1_out, minutes_set_enable, hours_set_enable);
  nand nand_1 (nand_1_out, or_1_out, direction_switch);
  and and_1 (and_1_out, action_button, hours_set_enable);
  or or_2 (or_2_out, and_1_out, and_2_out);
  Counter #(.max('h17), .width(5)) counter_1 (
    .clr(global_reset), .load(1'b0), .up(nand_1_out), .count(or_2_out), .clk(SIXTEEN_Hz_clock),
    .Q(current_time[10:6]));  // open: D, carry
  and and_2 (and_2_out, ~hours_set_enable, ONE_Hz_clock, seconds_carry, counter_2_carry);  // AND_Gate
  and and_3 (and_3_out, action_button, minutes_set_enable);
  or or_3 (or_3_out, and_3_out, and_4_out);
  Counter #(.max('h3b), .width(6)) counter_2 (
    .clr(global_reset), .load(1'b0), .up(nand_1_out), .count(or_3_out), .clk(SIXTEEN_Hz_clock),
    .carry(counter_2_carry), .Q(current_time[5:0]));  // open: D
  and and_4 (and_4_out, ~minutes_set_enable, seconds_carry, ONE_Hz_clock);  // AND_Gate
  Counter #(.max('h3b), .width(6)) seconds (
    .clr(global_reset), .load(1'b0), .count(ONE_Hz_clock), .clk(SIXTEEN_Hz_clock), .carry(seconds_carry));  // open: up, D, Q
  // Binary_to_BCD_converter #(.binvalue(6)) binary_to_bcd_converter_1: pin names not known; wires that end beside it: current_time[5:0], minutes_tens, minutes_units
  // Binary_to_BCD_converter #(.binvalue(5)) binary_to_bcd_converter_2: pin names not known; wires that end beside it: current_time[10:6], hours_tens, hours_units
endmodule

module fsm_state_decoder (
  input  [3:0] fsm_state_endoding,
  output clock_mode,
  output set_clock_hours_mode,
  output set_clock_minutes_mode,
  output set_alarm_hours_mode,
  output set_alarm_minutes_mode,
  output timer_idle_mode,
  output timer_run_mode,
  output countdown_set_minutes_mode,
  output countdown_set_seconds_mode,
  output countdown_idle_mode,
  output countdown_run_mode,
  output countdown_end_mode,
  output alarm_reached_mode
);

  and and_1 (clock_mode, ~fsm_state_endoding[0], ~fsm_state_endoding[1], ~fsm_state_endoding[2], ~fsm_state_endoding[3]);  // AND_Gate
  and and_2 (set_clock_hours_mode, fsm_state_endoding[0], ~fsm_state_endoding[1], ~fsm_state_endoding[2], ~fsm_state_endoding[3]);  // AND_Gate
  and and_3 (set_clock_minutes_mode, ~fsm_state_endoding[0], fsm_state_endoding[1], ~fsm_state_endoding[2], ~fsm_state_endoding[3]);  // AND_Gate
  and and_4 (set_alarm_hours_mode, fsm_state_endoding[0], fsm_state_endoding[1], ~fsm_state_endoding[2], ~fsm_state_endoding[3]);  // AND_Gate
  and and_5 (set_alarm_minutes_mode, ~fsm_state_endoding[0], ~fsm_state_endoding[1], fsm_state_endoding[2], ~fsm_state_endoding[3]);  // AND_Gate
  and and_6 (timer_idle_mode, fsm_state_endoding[0], ~fsm_state_endoding[1], fsm_state_endoding[2], ~fsm_state_endoding[3]);  // AND_Gate
  and and_7 (timer_run_mode, ~fsm_state_endoding[0], fsm_state_endoding[1], fsm_state_endoding[2], ~fsm_state_endoding[3]);  // AND_Gate
  and and_8 (countdown_set_minutes_mode, fsm_state_endoding[0], fsm_state_endoding[1], fsm_state_endoding[2], ~fsm_state_endoding[3]);  // AND_Gate
  and and_9 (countdown_set_seconds_mode, ~fsm_state_endoding[0], ~fsm_state_endoding[1], ~fsm_state_endoding[2], fsm_state_endoding[3]);  // AND_Gate
  and and_10 (countdown_idle_mode, fsm_state_endoding[0], ~fsm_state_endoding[1], ~fsm_state_endoding[2], fsm_state_endoding[3]);  // AND_Gate
  and and_11 (countdown_run_mode, ~fsm_state_endoding[0], fsm_state_endoding[1], ~fsm_state_endoding[2], fsm_state_endoding[3]);  // AND_Gate
  and and_12 (countdown_end_mode, fsm_state_endoding[0], fsm_state_endoding[1], ~fsm_state_endoding[2], fsm_state_endoding[3]);  // AND_Gate
  and and_13 (alarm_reached_mode, ~fsm_state_endoding[0], ~fsm_state_endoding[1], fsm_state_endoding[2], fsm_state_endoding[3]);  // AND_Gate
endmodule

module countdown_run_enable_sequential_logic (
  input  [3:0] next_mode,
  input  countdown_run_mode,
  input  SIXTEEN_Hz_clock,
  input  global_reset,
  output countdown_run_enable
);

  wire and_1_out, and_2_out, fsm_state_decoder_1_countdown_end_mode, fsm_state_decoder_1_countdown_idle_mode,
       fsm_state_decoder_1_countdown_run_mode, nor_1_out, or_1_out;

  fsm_state_decoder fsm_state_decoder_1 (
    .fsm_state_endoding(next_mode), .countdown_idle_mode(fsm_state_decoder_1_countdown_idle_mode),
    .countdown_run_mode(fsm_state_decoder_1_countdown_run_mode),
    .countdown_end_mode(fsm_state_decoder_1_countdown_end_mode));  // open: clock_mode, set_clock_hours_mode, set_clock_minutes_mode, set_alarm_hours_mode, set_alarm_minutes_mode, timer_idle_mode, timer_run_mode, countdown_set_minutes_mode, countdown_set_seconds_mode, alarm_reached_mode
  nor nor_1 (nor_1_out, fsm_state_decoder_1_countdown_idle_mode, fsm_state_decoder_1_countdown_end_mode);
  and and_1 (and_1_out, countdown_run_enable, nor_1_out);
  and and_2 (and_2_out, nor_1_out, countdown_run_mode);
  or or_1 (or_1_out, fsm_state_decoder_1_countdown_run_mode, and_1_out, and_2_out);
  D_Flip_Flop d_ff_1 (
    .D(or_1_out), .clk(SIXTEEN_Hz_clock), .Q(countdown_run_enable), .reset(global_reset));  // open: Qn, preset

  // Notes on the sheet:
  //   next mode = countdown idle or countdown end
  //   current mode = countdown run
  //   next mode = countdown run
endmodule

module display_module (
  input  [3:0] tens_2nd,
  input  [3:0] units_2nd,
  input  [3:0] tens_1st,
  input  [3:0] units_1st,
  input  [1:0] display_mode,
  input  [1:0] alarm_countdown_end,
  input  flash_2,
  input  flash_1,
  output [6:0] tens_2nd_7dig,
  output [6:0] units_2nd_7dig,
  output [6:0] tens_1st_7dig,
  output [6:0] units_1st_7dig,
  output [6:0] label_2nd,
  output [6:0] label_1st
);

  wire and_1_out, or_1_out;
  wire [1:0] multiplexer_3_out, multiplexer_8_out, multiplexer_13_out;
  wire [2:0] multiplexer_12_out, multiplexer_15_out;
  wire [3:0] multiplexer_1_out, multiplexer_5_out, multiplexer_7_out, multiplexer_9_out;

  Multiplexer #(.select(2), .width(4)) multiplexer_1 (
    .in0(tens_2nd), .in1(4'b1101), .in2(4'b1110), .in3(4'b1111), .out(multiplexer_1_out),
    .sel(multiplexer_3_out));
  Multiplexer #(.select(4), .width(7)) multiplexer_2 (
    .in0(7'b1111110), .in1(7'b0011000), .in2(7'b1101101), .in3(7'b0111101), .in4(7'b0011011),
    .in5(7'b0110111), .in6(7'b1110111), .in7(7'b0011100), .in8({7{1'b1}}), .in9(7'b0111111),
    .in13(7'b0000001), .in14(7'b0000001), .in15({7{1'b0}}), .out(tens_2nd_7dig), .sel(multiplexer_1_out));  // open: in10, in11, in12
  Multiplexer #(.width(2)) multiplexer_3 (
    .in0(alarm_countdown_end), .in1({2{flash_2}}), .out(multiplexer_3_out), .sel(flash_2));
  Multiplexer #(.select(4), .width(7)) multiplexer_4 (
    .in0(7'b1111110), .in1(7'b0011000), .in2(7'b1101101), .in3(7'b0111101), .in4(7'b0011011),
    .in5(7'b0110111), .in6(7'b1110111), .in7(7'b0011100), .in8({7{1'b1}}), .in9(7'b0111111),
    .in13(7'b0000001), .in14(7'b0000001), .in15({7{1'b0}}), .out(units_2nd_7dig), .sel(multiplexer_5_out));  // open: in10, in11, in12
  Multiplexer #(.select(2), .width(4)) multiplexer_5 (
    .in0(units_2nd), .in1(4'b1101), .in2(4'b1110), .in3(4'b1111), .out(multiplexer_5_out),
    .sel(multiplexer_3_out));
  Multiplexer #(.select(4), .width(7)) multiplexer_6 (
    .in0(7'b1111110), .in1(7'b0011000), .in2(7'b1101101), .in3(7'b0111101), .in4(7'b0011011),
    .in5(7'b0110111), .in6(7'b1110111), .in7(7'b0011100), .in8({7{1'b1}}), .in9(7'b0111111),
    .in13(7'b1011111), .in14(7'b1100110), .in15({7{1'b0}}), .out(tens_1st_7dig), .sel(multiplexer_7_out));  // open: in10, in11, in12
  Multiplexer #(.select(2), .width(4)) multiplexer_7 (
    .in0(tens_1st), .in1(4'b1101), .in2(4'b1110), .in3(4'b1111), .out(multiplexer_7_out),
    .sel(multiplexer_8_out));
  Multiplexer #(.width(2)) multiplexer_8 (
    .in0(alarm_countdown_end), .in1({2{flash_1}}), .out(multiplexer_8_out), .sel(flash_1));
  Multiplexer #(.select(2), .width(4)) multiplexer_9 (
    .in0(units_1st), .in1(4'b1101), .in2(4'b1110), .in3(4'b1111), .out(multiplexer_9_out),
    .sel(multiplexer_8_out));
  Multiplexer #(.select(4), .width(7)) multiplexer_10 (
    .in0(7'b1111110), .in1(7'b0011000), .in2(7'b1101101), .in3(7'b0111101), .in4(7'b0011011),
    .in5(7'b0110111), .in6(7'b1110111), .in7(7'b0011100), .in8({7{1'b1}}), .in9(7'b0111111),
    .in13(7'b1100010), .in14(7'b1100011), .in15({7{1'b0}}), .out(units_1st_7dig), .sel(multiplexer_9_out));  // open: in10, in11, in12
  and and_1 (and_1_out, flash_1, or_1_out);
  or or_1 (or_1_out, alarm_countdown_end[0], alarm_countdown_end[1]);
  Multiplexer #(.select(3), .width(7)) multiplexer_11 (
    .in0(7'b1100010), .in1(7'b1100010), .in2({7{1'b0}}), .in3(7'b1100011), .in5(7'b0000001),
    .in6(7'b0000001), .in7({7{1'b0}}), .out(label_2nd), .sel(multiplexer_12_out));  // open: in4
  Multiplexer #(.select(2), .width(3)) multiplexer_12 (
    .in0({1'b0, display_mode}), .in1(3'b101), .in2(3'b110), .in3(3'b111), .out(multiplexer_12_out),
    .sel(multiplexer_13_out));
  Multiplexer #(.width(2)) multiplexer_13 (
    .in0(alarm_countdown_end), .in1({2{flash_1}}), .out(multiplexer_13_out), .sel(and_1_out));
  Multiplexer #(.select(3), .width(7)) multiplexer_14 (
    .in0(7'b1100110), .in1(7'b1011111), .in2(7'b1100011), .in3(7'b1100110), .in5(7'b0000001),
    .in6(7'b0000001), .in7({7{1'b0}}), .out(label_1st), .sel(multiplexer_15_out));  // open: in4
  Multiplexer #(.select(2), .width(3)) multiplexer_15 (
    .in0({1'b0, display_mode}), .in1(3'b101), .in2(3'b110), .in3(3'b111), .out(multiplexer_15_out),
    .sel(multiplexer_13_out));

  // Notes on the sheet:
  //   0 = 1111110
  //   1 = 0011000
endmodule

module timer_module (
  input  timer_run_enable,
  input  local_reset_switch,
  input  global_reset,
  input  ONE_Hz_clock,
  output [3:0] seconds_tens,
  output [3:0] seconds_units,
  output [3:0] minutes_tens,
  output [3:0] minutes_units
);

  wire and_1_out, counter_2_carry, or_1_out;
  wire [4:0] counter_1_q;
  wire [5:0] counter_2_q;

  or or_1 (or_1_out, local_reset_switch, global_reset);
  and and_1 (and_1_out, timer_run_enable, counter_2_carry);
  Counter #(.max('h1b), .width(5)) counter_1 (
    .clr(or_1_out), .load(1'b0), .up(1'b1), .count(and_1_out), .clk(ONE_Hz_clock), .Q(counter_1_q));  // open: D, carry
  Counter #(.max('h3b), .width(6)) counter_2 (
    .clr(or_1_out), .load(1'b0), .up(1'b1), .count(timer_run_enable), .clk(ONE_Hz_clock),
    .carry(counter_2_carry), .Q(counter_2_q));  // open: D
  // Binary_to_BCD_converter #(.binvalue(6)) binary_to_bcd_converter_1: pin names not known; wires that end beside it: counter_2_q, seconds_tens, seconds_units
  // Binary_to_BCD_converter #(.binvalue(5)) binary_to_bcd_converter_2: pin names not known; wires that end beside it: counter_1_q, minutes_tens, minutes_units
endmodule

module SR_Pulse (
  input  S,
  input  global_reset,
  input  high_clock,
  input  low_clock,
  output O
);

  wire d_ff_1_q, d_ff_2_q, s_r_ff_1_q;

  S_R_Flip_Flop s_r_ff_1 (
    .S(S), .R(d_ff_2_q), .clk(high_clock), .Q(s_r_ff_1_q), .reset(global_reset));  // open: Qn, preset
  D_Flip_Flop d_ff_1 (.D(s_r_ff_1_q), .clk(low_clock), .Q(d_ff_1_q), .reset(global_reset));  // open: Qn, preset
  D_Flip_Flop d_ff_2 (.D(d_ff_1_q), .clk(low_clock), .Q(d_ff_2_q), .reset(global_reset));  // open: Qn, preset
  and and_1 (O, d_ff_1_q, ~d_ff_2_q);  // AND_Gate
endmodule

module SR_Sync (
  input  S,
  input  global_reset,
  input  high_clock,
  input  low_clock,
  output O
);

  wire and_1_out, d_ff_2_q, s_r_ff_1_q;

  and and_1 (and_1_out, ~d_ff_2_q, S);  // AND_Gate
  S_R_Flip_Flop s_r_ff_1 (
    .S(and_1_out), .R(O), .clk(high_clock), .Q(s_r_ff_1_q), .reset(global_reset));  // open: Qn, preset
  D_Flip_Flop d_ff_1 (.D(s_r_ff_1_q), .clk(low_clock), .Q(O), .reset(global_reset));  // open: Qn, preset
  D_Flip_Flop d_ff_2 (.D(O), .clk(low_clock), .Q(d_ff_2_q), .reset(global_reset));  // open: Qn, preset
endmodule

module countdown_module (
  input  action_button,
  input  direction_switch,
  input  minutes_set_enable,
  input  seconds_set_enable,
  input  countdown_run_enable,
  input  global_reset,
  input  ONE_Hz_clock,
  input  SIXTEEN_Hz_clock,
  output countdown_end,
  output [3:0] seconds_tens,
  output [3:0] seconds_units,
  output [3:0] minutes_tens,
  output [3:0] minutes_units
);

  wire and_1_out, and_2_out, and_3_out, and_4_out, and_5_out, comparator_1_eq, counter_2_carry, nor_1_out,
       or_1_out, or_2_out, or_3_out;
  wire [5:0] counter_1_q, counter_2_q;

  or or_1 (or_1_out, seconds_set_enable, minutes_set_enable);
  and and_1 (and_1_out, or_1_out, direction_switch);
  and and_2 (and_2_out, action_button, minutes_set_enable);
  or or_2 (or_2_out, and_2_out, and_3_out);
  Counter #(.max('h3b), .width(6)) counter_1 (
    .clr(global_reset), .load(1'b0), .up(nor_1_out), .count(or_2_out), .clk(SIXTEEN_Hz_clock), .Q(counter_1_q));  // open: D, carry
  nor nor_1 (nor_1_out, countdown_run_enable, and_1_out);
  and and_3 (and_3_out, countdown_run_enable, ~countdown_end, ONE_Hz_clock, counter_2_carry);  // AND_Gate
  and and_4 (and_4_out, action_button, seconds_set_enable);
  or or_3 (or_3_out, and_4_out, and_5_out);
  Counter #(.max('h3b), .width(6)) counter_2 (
    .clr(global_reset), .load(1'b0), .up(nor_1_out), .count(or_3_out), .clk(SIXTEEN_Hz_clock),
    .carry(counter_2_carry), .Q(counter_2_q));  // open: D
  and and_5 (and_5_out, countdown_run_enable, ~countdown_end, ONE_Hz_clock);  // AND_Gate
  // Binary_to_BCD_converter #(.binvalue(6)) binary_to_bcd_converter_1: pin names not known; wires that end beside it: counter_2_q, seconds_tens, seconds_units
  // Binary_to_BCD_converter #(.binvalue(6)) binary_to_bcd_converter_2: pin names not known; wires that end beside it: counter_1_q, minutes_tens, minutes_units
  Comparator #(.width(12)) comparator_1 (
    .a({12{1'b0}}), .b({counter_1_q, counter_2_q}), .eq(comparator_1_eq));  // open: gt, lt
  and and_6 (countdown_end, countdown_run_enable, comparator_1_eq);

  // Notes on the sheet:
  //   removed not(minutes set enable) as input into the auto_enable gates since whats relevant is onlz countdown_run_enable
endmodule

module alarm_module (
  input  action_button,
  input  direction_switch,
  input  alarm_active,
  input  [10:0] current_time,
  input  hours_set_enable,
  input  minutes_set_enable,
  input  global_reset,
  input  SIXTEEN_Hz_clock,
  output alarm_end,
  output [3:0] minutes_tens,
  output [3:0] minutes_units,
  output [3:0] hours_tens,
  output [3:0] hours_units
);

  wire and_1_out, and_2_out, comparator_1_eq, nand_1_out, or_1_out;
  wire [5:0] counter_2_q;
  wire [10:6] counter_1_q;

  or or_1 (or_1_out, minutes_set_enable, hours_set_enable);
  and and_1 (and_1_out, action_button, hours_set_enable);
  Counter #(.max('h17), .width(5)) counter_1 (
    .clr(global_reset), .load(1'b0), .up(nand_1_out), .count(and_1_out), .clk(SIXTEEN_Hz_clock),
    .Q(counter_1_q));  // open: D, carry
  nand nand_1 (nand_1_out, or_1_out, direction_switch);
  and and_2 (and_2_out, action_button, minutes_set_enable);
  Counter #(.max('h3b), .width(6)) counter_2 (
    .clr(global_reset), .load(1'b0), .up(nand_1_out), .count(and_2_out), .clk(SIXTEEN_Hz_clock),
    .Q(counter_2_q));  // open: D, carry
  // Binary_to_BCD_converter #(.binvalue(6)) binary_to_bcd_converter_1: pin names not known; wires that end beside it: counter_2_q, minutes_tens, minutes_units
  // Binary_to_BCD_converter #(.binvalue(5)) binary_to_bcd_converter_2: pin names not known; wires that end beside it: counter_1_q, hours_tens, hours_units
  Comparator #(.width(11)) comparator_1 (
    .a(current_time), .b({counter_1_q, counter_2_q}), .eq(comparator_1_eq));  // open: gt, lt
  and and_3 (alarm_end, alarm_active, comparator_1_eq);
endmodule

module display_mux (
  input  [15:0] hour_in,
  input  [15:0] alarm_in,
  input  [15:0] timer_in,
  input  [15:0] countdown_in,
  input  [4:0] countdown_modes,
  input  [1:0] timer_modes,
  input  [2:0] alarm_modes,
  input  [1:0] hour_modes,
  input  flash_clock,
  input  action,
  output [15:0] display_signal,
  output [1:0] display_mode,
  output [1:0] alarm_countdown_end,
  output flash_2,
  output flash_1
);

  wire or_5_out, or_6_out;
  wire [1:0] or_3_out;
  wire [1:1] or_1_out;

  or or_1 (or_1_out[1], countdown_modes[0], countdown_modes[1], countdown_modes[2], countdown_modes[3], countdown_modes[4]);
  or or_2 (or_3_out[1], timer_modes[0], timer_modes[1]);
  or or_3 (or_3_out[0], alarm_modes[0], alarm_modes[1], alarm_modes[2]);
  Multiplexer #(.select(2), .width(16)) multiplexer_1 (
    .in0(hour_in), .in1(alarm_in), .in2(timer_in), .in3(countdown_in), .out(display_signal),
    .sel(display_mode));
  assign display_mode = {2{or_1_out[1]}} | or_3_out;  // OR_Gate or_4, 2 bits wide
  or or_5 (or_5_out, alarm_modes[2], countdown_modes[4], hour_modes[1], alarm_modes[0], countdown_modes[1]);
  or or_6 (or_6_out, alarm_modes[2], countdown_modes[4], hour_modes[0], alarm_modes[1], countdown_modes[0]);
  and and_1 (flash_2, or_5_out, ~action, flash_clock);  // AND_Gate
  and and_2 (flash_1, or_6_out, ~action, flash_clock);  // AND_Gate

  assign alarm_countdown_end = {countdown_modes[4], alarm_modes[2]};
endmodule

module buzzer_module (
  input  alarm_reached_mode,
  input  countdown_end_mode,
  output buzzer_signal
);

  wire clock_1_out, or_1_out;

  or or_1 (or_1_out, alarm_reached_mode, countdown_end_mode);
  Clock #(.highDuration(384), .lowDuration(384)) clock_1 (.out(clock_1_out));
  T_Flip_Flop t_ff_1 (.T(or_1_out), .clk(clock_1_out), .Q(buzzer_signal));  // open: Qn, reset, preset
endmodule
